# Fritzing sketch wiringDiagram (saved by Fritzing 1.0.2b)
breadboards: 1

parts:
  A1 = ESP32 DOIT DEVKIT V1 36pin
  LED2 = smd LED [color="Blue (430nm)" package="1206 [SMD]"]
  LED3 = smd LED [color="Green (555nm)" package="0603 [SMD]"]
  LED4 = smd LED [color="Red (633nm)" package="0805 [SMD]"]
  LED5 = smd LED [color="Yellow (595nm)" package="0805 [SMD]"]
  Joystick = Thumb Joystick
  R5 = Resistor [tolerance=±5% resistance=220 package="2010 [SMD]"]
  R7 = Resistor [tolerance=±5% resistance=220 package="2010 [SMD]"]
  R8 = Resistor [tolerance=±5% resistance=220 package="2010 [SMD]"]
  R9 = Resistor [tolerance=±5% resistance=220 package="2010 [SMD]"]

nets:
  N1: A1.Pin_19, Joystick.VCC
  N2: A1.Pin_20, Joystick.GND, R5.Pin_1, R7.Pin_1, R8.Pin_1, R9.Pin_1
  N3: A1.Pin_21, Joystick.HORZ
  N4: A1.Pin_22, Joystick.VERT
  N5: A1.Pin_23, Joystick.SEL
  N6: A1.Pin_24, LED5.anode
  N7: A1.Pin_25, LED4.anode
  N8: A1.Pin_26, LED2.anode
  N9: A1.Pin_27, LED3.anode
  N10: LED2.cathode, R7.Pin_0
  N11: LED3.cathode, R5.Pin_0
  N12: LED4.cathode, R8.Pin_0
  N13: LED5.cathode, R9.Pin_0

custom parts:
  ESP32 DOIT DEVKIT V1 36pin: ESP32 DOIT DEVKIT V1 36pin.
